# Fritzing sketch Fairytale (saved by Fritzing 0.9.3b)
breadboards: 1

parts:
  Arduino_UNO_V3 = Arduino Uno (Rev3)
  Sparkfun_PN532_NFC_Breakout_Board = Adafruit PN532 Breakout [part_number="Adafruit #364"]
  MP3_Player = Adafruit Music Maker Shield with Amp [part_number="Adafruit #1788"]
  Powerboost = PowerBoost 1000 Basic
  Potentiometer = Rotary Potentiometer (Small) [maximum_resistance=100kΩ package=THT]  # not connected
  Pause-Button = Pushbutton [package="[THT]"]
  Prev-Button = Pushbutton [package="[THT]"]
  Next-Button = Pushbutton [package="[THT]"]
  Light-Button = Pushbutton [package="[THT]"]
  Programming-Button = Square Pushbutton  # not connected
  R1 = Resistor [tolerance=±5% resistance=330 package="2512 [SMD]"]
  R2 = Resistor [tolerance=±5% resistance=220 package="2512 [SMD]"]  # not connected
  R3 = Resistor [tolerance=±5% resistance=220 package="1206 [SMD]"]  # not connected
  R4 = Resistor [tolerance=±5% resistance=220 package="1206 [SMD]"]  # not connected
  R5 = Resistor [tolerance=±5% resistance=220 package="0603 [SMD]"]
  R6 = Resistor [tolerance=±5% resistance=1k package="0402 [SMD]"]
  R7 = Resistor [tolerance=±5% resistance=33 package="0805 [SMD]"]
  R8 = Resistor [tolerance=±5% resistance=10k package=THT]  # not connected
  Speaker = SPEAKER [package=pcb_mount_speaker]
  Battery = Lithium Ion Polymer Battery 3.7v 2500mAh [part_number=328]
  Operations-LED = LED - 3mm [color="Blue (525nm)" package="3 mm [THT]"]  # not connected
  Error-LED = LED - 3mm [color="Red (633nm)" package="3 mm [THT]"]  # not connected
  Warning-LED = LED - 3mm [color="Yellow (595nm)" package="3 mm [THT]"]  # not connected

nets:
  N1: Arduino_UNO_V3.D10_PWM/SS, Sparkfun_PN532_NFC_Breakout_Board.NSS/SCL/RX
  N2: Arduino_UNO_V3.D11_PWM/MOSI, Sparkfun_PN532_NFC_Breakout_Board.MOSI/SDA/TX, MP3_Player.MOSI_ICSP
  N3: Arduino_UNO_V3.D12/MISO, Sparkfun_PN532_NFC_Breakout_Board.MISO, MP3_Player.MISO_ICSP
  N4: Arduino_UNO_V3.D13/SCK, Sparkfun_PN532_NFC_Breakout_Board.SCK, MP3_Player.SCK_ICSP
  N5: Arduino_UNO_V3.D3_PWM, MP3_Player.DREQ
  N6: Arduino_UNO_V3.D4, MP3_Player.SD_CS
  N7: Arduino_UNO_V3.D7, MP3_Player.XDCS
  N8: Arduino_UNO_V3.RESET, MP3_Player.RESET_ICSP
  N9: MP3_Player.LEFT-, Speaker.-
  N10: MP3_Player.LEFT+, Speaker.+
  GND: MP3_Player.GND, Powerboost.GND
  N11: Powerboost.VBAT, Battery.positive
  N12: Pause-Button.Pin_3, Pause-Button.Pin_4, R6.Pin_0
  N13: Prev-Button.Pin_3, Prev-Button.Pin_4, R1.Pin_0
  N14: Next-Button.Pin_3, Next-Button.Pin_4, R5.Pin_0
  N15: Light-Button.Pin_3, Light-Button.Pin_4, R7.Pin_0
  5V: R1.Pin_1, R5.Pin_1, R6.Pin_1, R7.Pin_1

custom parts:
  Adafruit PN532 Breakout: The PN532 is the most popular NFC chip, and is what is embedded in pretty much every phone or device that does NFC. It can pretty much do it all, such as read and write to tags and cards, communicate with phones (say for payment processing), and 'act' like a NFC tag. If you want to do any sort of embedded NFC work, this is the chip you'll want to use! NFC (Near Field Communications) is a way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
  Adafruit Music Maker Shield with Amp: Bend all audio files to your will with the Adafruit Music Maker shield for Arduino! This powerful shield features the VS1053, an encoding/decoding (codec) chip that can decode a wide variety of audio formats such as MP3, AAC, Ogg Vorbis, WMA, MIDI, FLAC, WAV (PCM and ADPCM). It can also be used to record audio in both PCM (WAV) and compressed Ogg Vorbis. You can do all sorts of stuff with the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
  PowerBoost 1000 Basic: The PowerBoost 1000 is a little DC/DC boost converter module that can run from 1.8V batteries or higher, and convert the battery output to 5.2V DC for running your 5V projects. At its heart is a TPS61030 boost converter from TI. This boost converter chip has some really nice extras such as low battery detection, 4A internal switch, synchronous conversion, excellent efficiency, and 700KHz high-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
  Lithium Ion Polymer Battery 3.7v 2500mAh: Lithium ion polymer (also known as 'lipo' or 'lipoly') batteries are thin, light and powerful. The output ranges from 4.2V when completely charged to 3.7V. This battery has a capacity of 2500mAh for a total of about 10 Wh. The batteries come pre-attached with a genuine 2-pin JST-PH connector as shown and include the necessary protection circuitry.
